// Logisim project lab2_adv.circ as structural Verilog: 1 circuit, main circuit multiplier
module multiplier (
  input  [3:0] a,
  input  [3:0] b,
  output [7:0] p
);

  wire [2:0] and_2_out;
  wire [3:0] and_5_out, and_9_out, and_13_out;
  wire [3:1] adder_1_out, adder_2_out;
  wire [3:3] adder_1_cout, adder_2_cout;

  and and_1 (p[0], a[0], b[0]);
  and and_2 (and_2_out[0], a[1], b[0]);
  and and_3 (and_2_out[1], a[2], b[0]);
  and and_4 (and_2_out[2], a[3], b[0]);
  and and_5 (and_5_out[0], a[0], b[1]);
  and and_6 (and_5_out[1], a[1], b[1]);
  and and_7 (and_5_out[2], a[2], b[1]);
  and and_8 (and_5_out[3], a[3], b[1]);
  and and_9 (and_9_out[0], a[0], b[2]);
  and and_10 (and_9_out[1], a[1], b[2]);
  and and_11 (and_9_out[2], a[2], b[2]);
  and and_12 (and_9_out[3], a[3], b[2]);
  and and_13 (and_13_out[0], a[0], b[3]);
  and and_14 (and_13_out[1], a[1], b[3]);
  and and_15 (and_13_out[2], a[2], b[3]);
  and and_16 (and_13_out[3], a[3], b[3]);
  Adder #(.width(4)) adder_1 (
    .a({1'b0, and_2_out}), .b(and_5_out), .out({adder_1_out, p[1]}), .cout(adder_1_cout[3]));  // open: cin
  Adder #(.width(4)) adder_2 (
    .a({adder_1_cout[3], adder_1_out}), .b(and_9_out), .out({adder_2_out, p[2]}), .cout(adder_2_cout[3]));  // open: cin
  Adder #(.width(4)) adder_3 (
    .a({adder_2_cout[3], adder_2_out}), .b(and_13_out), .out(p[6:3]), .cout(p[7]));  // open: cin
endmodule
